// Logisim project CPU_MIGS.circ as structural Verilog: 5 circuits, main circuit main
module main (
  input  in_1,
  output out_2
);

  wire and_1_out, comparator_1_eq, multiplexer_2_out, not_1_out, pull_resistor_1_node,
       unidade_de_controle_1_jmp, unidade_de_controle_1_lda, unidade_de_controle_1_ldi,
       unidade_de_controle_1_mov, unidade_de_controle_1_str;
  wire [3:0] multiplexer_5_out, multiplexer_7_out, multiplexer_9_out, \ula_1_endereço_r0 ,
       unidade_de_controle_1_aluop, unidade_de_controle_1_rx, unidade_de_controle_1_ry;
  wire [7:0] adder_1_out, banco_de_registradores_1_rx, banco_de_registradores_1_ry, multiplexer_1_out,
       multiplexer_3_out, multiplexer_4_out, multiplexer_6_out, multiplexer_8_out, ram_2_data,
       \registrador_1_saída , subtractor_1_out, ula_1_resultado, undriven, unidade_de_controle_1_ldi_value,
       unidade_de_controle_1_out_12;
  wire [11:0] ram_1_data;

  Registrador registrador_1 (.ENTRADA(multiplexer_1_out), .CLOCK(in_1), .\SAÍDA (\registrador_1_saída ));
  Multiplexer #(.width(8)) multiplexer_1 (
    .in0(adder_1_out), .in1(unidade_de_controle_1_out_12), .out(multiplexer_1_out), .sel(and_1_out),
    .en(not_1_out));
  RAM #(.dataWidth(12)) ram_1 (.addr(undriven), .data(ram_1_data), .ld(1'b1));  // open: sel, clk, clr
  and and_1 (and_1_out, unidade_de_controle_1_jmp, comparator_1_eq);
  Comparator comparator_1 (.a(banco_de_registradores_1_rx), .b(8'h1), .eq(comparator_1_eq));  // open: gt, lt
  not not_1 (not_1_out, pull_resistor_1_node);
  Multiplexer multiplexer_2 (.in0(in_1), .in1(1'b0), .out(multiplexer_2_out), .sel(pull_resistor_1_node));  // open: en
  Pull_Resistor pull_resistor_1 (.node(pull_resistor_1_node));
  Adder adder_1 (.a(8'h1), .b(\registrador_1_saída ), .out(adder_1_out));  // open: cin, cout
  Subtractor subtractor_1 (.a(undriven), .b(8'h1), .out(subtractor_1_out));  // open: bin, bout
  Unidade_de_Controle unidade_de_controle_1 (
    .\instrução (ram_1_data), .Aluop(unidade_de_controle_1_aluop), .Rx(unidade_de_controle_1_rx),
    .Ry(unidade_de_controle_1_ry), .LDI_Value(unidade_de_controle_1_ldi_value),
    .out_12(unidade_de_controle_1_out_12), .LDA(unidade_de_controle_1_lda), .LDI(unidade_de_controle_1_ldi),
    .STR(unidade_de_controle_1_str), .MOV(unidade_de_controle_1_mov), .JMP(unidade_de_controle_1_jmp),
    .HLT(pull_resistor_1_node));
  ULA ula_1 (
    .zero(out_2), .Rx(banco_de_registradores_1_rx), .Resultado(ula_1_resultado),
    .Ry(banco_de_registradores_1_ry), .Aluop(unidade_de_controle_1_aluop), .\Endereço_R0 (\ula_1_endereço_r0 ));
  Multiplexer #(.width(8)) multiplexer_3 (
    .in0(ula_1_resultado), .in1(subtractor_1_out), .out(multiplexer_3_out), .sel(unidade_de_controle_1_jmp));  // open: en
  Multiplexer #(.width(8)) multiplexer_4 (
    .in0(multiplexer_3_out), .in1(unidade_de_controle_1_ldi_value), .out(multiplexer_4_out),
    .sel(unidade_de_controle_1_ldi));  // open: en
  Multiplexer #(.width(4)) multiplexer_5 (
    .in0(\ula_1_endereço_r0 ), .in1(4'b1111), .out(multiplexer_5_out), .sel(unidade_de_controle_1_jmp));  // open: en
  Multiplexer #(.width(8)) multiplexer_6 (
    .in0(multiplexer_4_out), .in1(banco_de_registradores_1_ry), .out(multiplexer_6_out),
    .sel(unidade_de_controle_1_mov));  // open: en
  Multiplexer #(.width(4)) multiplexer_7 (
    .in0(multiplexer_5_out), .in1(unidade_de_controle_1_rx), .out(multiplexer_7_out),
    .sel(unidade_de_controle_1_mov));  // open: en
  Multiplexer #(.width(8)) multiplexer_8 (
    .in0(multiplexer_6_out), .in1(ram_2_data), .out(multiplexer_8_out), .sel(unidade_de_controle_1_lda));  // open: en
  Multiplexer #(.width(4)) multiplexer_9 (
    .in0(multiplexer_7_out), .in1(4'b0000), .out(multiplexer_9_out), .sel(unidade_de_controle_1_lda));  // open: en
  RAM #(.bus("separate")) ram_2 (
    .addr(unidade_de_controle_1_out_12), .din(banco_de_registradores_1_rx), .data(ram_2_data),
    .str(unidade_de_controle_1_str), .clk(multiplexer_2_out), .ld(unidade_de_controle_1_lda));  // open: sel, clr
  Banco_de_Registradores banco_de_registradores_1 (
    .Data_IN(multiplexer_8_out), .write(multiplexer_2_out), .write_select(multiplexer_9_out),
    .Rx(banco_de_registradores_1_rx), .Rx_Select(unidade_de_controle_1_rx), .Ry(banco_de_registradores_1_ry),
    .Ry_Select(unidade_de_controle_1_ry));

  // Notes on the sheet:
  //   PC
  //   IR
  //   DATA MEM
endmodule

module ULA (
  input  [7:0] Rx,
  input  [7:0] Ry,
  input  [3:0] Aluop,
  output [7:0] Resultado,
  output [3:0] \Endereço_R0 ,
  output zero
);

  wire comparator_1_eq, comparator_1_gt, comparator_1_lt;
  wire [7:0] adder_1_out, and_1_out, bit_extender_1_out, divider_1_out, multiplier_1_out, negator_1_out,
       or_1_out, subtractor_1_out;

  Negator negator_1 (.in(Rx), .out(negator_1_out));
  Adder adder_1 (.a(Rx), .b(Ry), .out(adder_1_out));  // open: cin, cout
  Subtractor subtractor_1 (.a(Rx), .b(Ry), .out(subtractor_1_out));  // open: bin, bout
  Multiplier multiplier_1 (.a(Rx), .b(Ry), .out(multiplier_1_out));  // open: cin, cout
  Divider divider_1 (.a(Rx), .b(Ry), .out(divider_1_out));  // open: upper, rem
  Comparator comparator_1 (.a(Rx), .b(Ry), .gt(comparator_1_gt), .eq(comparator_1_eq), .lt(comparator_1_lt));
  assign and_1_out = Rx & Ry;  // AND_Gate and_1, 8 bits wide
  assign or_1_out = Rx | Ry;  // OR_Gate or_1, 8 bits wide
  Multiplexer #(.select(4), .width(8)) multiplexer_1 (
    .in0(and_1_out), .in1(or_1_out), .in2(negator_1_out), .in3(adder_1_out), .in4(subtractor_1_out),
    .in5(multiplier_1_out), .in6(divider_1_out), .in7(bit_extender_1_out), .in8(bit_extender_1_out),
    .in9(bit_extender_1_out), .out(Resultado), .sel(Aluop));  // open: in10, in11, in12, in13, in14, in15, en
  Multiplexer #(.select(4)) multiplexer_2 (
    .in7(comparator_1_eq), .in8(comparator_1_lt), .in9(comparator_1_gt), .out(zero), .sel(Aluop));  // open: in0, in1, in2, in3, in4, in5, in6, in10, in11, in12, in13, in14, in15, en
  assign bit_extender_1_out = {{7{1'b0}}, zero};  // Bit_Extender bit_extender_1

  assign \Endereço_R0  = 4'b0000;
endmodule

module Unidade_de_Controle (
  input  [11:0] \instrução ,
  output LDA,
  output LDI,
  output STR,
  output MOV,
  output JMP,
  output HLT,
  output [3:0] Aluop,
  output [3:0] Rx,
  output [3:0] Ry,
  output [7:0] LDI_Value,
  output [7:0] out_12
);

  wire multiplexer_1_out, or_1_out;

  Multiplexer #(.select(4)) multiplexer_1 (
    .in0(1'b0), .in1(1'b0), .in2(1'b0), .in3(1'b0), .in4(1'b0), .in5(1'b0), .in6(1'b0), .in7(1'b0),
    .in8(1'b0), .in9(1'b0), .in10(1'b1), .in11(1'b1), .in12(1'b1), .in13(1'b1), .in14(1'b1), .in15(1'b1),
    .out(multiplexer_1_out), .sel(\instrução [11:8]));  // open: en
  Demultiplexer #(.select(4)) demultiplexer_1 (
    .out10(LDA), .out11(LDI), .out12(STR), .out13(MOV), .out14(JMP), .out15(HLT), .in(multiplexer_1_out),
    .sel(\instrução [11:8]));  // open: out0, out1, out2, out3, out4, out5, out6, out7, out8, out9, en
  or or_1 (or_1_out, JMP, STR);
  Multiplexer #(.width(4)) multiplexer_2 (.in0(\instrução [7:4]), .in1(4'b0000), .out(Rx), .sel(or_1_out));  // open: en
  Pull_Resistor pull_resistor_1 (.node(LDA));
  Pull_Resistor pull_resistor_2 (.node(STR));
  Pull_Resistor pull_resistor_3 (.node(JMP));

  assign Aluop = \instrução [11:8];
  assign LDI_Value = \instrução [7:0];
  assign out_12 = \instrução [7:0];
  assign Ry = \instrução [3:0];
endmodule

module Registrador (
  input  [7:0] ENTRADA,
  input  CLOCK,
  output [7:0] \SAÍDA 
);

  D_Flip_Flop d_ff_1 (.clk(CLOCK), .D(ENTRADA[7]), .Q(\SAÍDA [7]));  // open: Qn, preset, en, reset
  D_Flip_Flop d_ff_2 (.clk(CLOCK), .D(ENTRADA[6]), .Q(\SAÍDA [6]));  // open: Qn, preset, en, reset
  D_Flip_Flop d_ff_3 (.clk(CLOCK), .D(ENTRADA[5]), .Q(\SAÍDA [5]));  // open: Qn, preset, en, reset
  D_Flip_Flop d_ff_4 (.clk(CLOCK), .D(ENTRADA[4]), .Q(\SAÍDA [4]));  // open: Qn, preset, en, reset
  D_Flip_Flop d_ff_5 (.clk(CLOCK), .D(ENTRADA[3]), .Q(\SAÍDA [3]));  // open: Qn, preset, en, reset
  D_Flip_Flop d_ff_6 (.clk(CLOCK), .D(ENTRADA[2]), .Q(\SAÍDA [2]));  // open: Qn, preset, en, reset
  D_Flip_Flop d_ff_7 (.clk(CLOCK), .D(ENTRADA[1]), .Q(\SAÍDA [1]));  // open: Qn, preset, en, reset
  D_Flip_Flop d_ff_8 (.clk(CLOCK), .D(ENTRADA[0]), .Q(\SAÍDA [0]));  // open: Qn, preset, en, reset
endmodule

module Banco_de_Registradores (
  input  [3:0] Rx_Select,
  input  [7:0] Data_IN,
  input  [3:0] Ry_Select,
  input  write,
  input  [3:0] write_select,
  output [7:0] Rx,
  output [7:0] Ry
);

  wire demultiplexer_1_out0, demultiplexer_1_out1, demultiplexer_1_out2, demultiplexer_1_out3,
       demultiplexer_1_out4, demultiplexer_1_out5, demultiplexer_1_out6, demultiplexer_1_out7,
       demultiplexer_1_out8, demultiplexer_1_out9, demultiplexer_1_out10, demultiplexer_1_out11,
       demultiplexer_1_out12, demultiplexer_1_out13, demultiplexer_1_out14, demultiplexer_1_out15;
  wire [7:0] \registrador_1_saída , \registrador_2_saída , \registrador_3_saída , \registrador_4_saída ,
       \registrador_5_saída , \registrador_6_saída , \registrador_7_saída , \registrador_8_saída ,
       \registrador_9_saída , \registrador_10_saída , \registrador_11_saída , \registrador_12_saída ,
       \registrador_13_saída , \registrador_14_saída , \registrador_15_saída , \registrador_16_saída ;

  Demultiplexer #(.select(4)) demultiplexer_1 (
    .out0(demultiplexer_1_out0), .out1(demultiplexer_1_out1), .out2(demultiplexer_1_out2),
    .out3(demultiplexer_1_out3), .out4(demultiplexer_1_out4), .out5(demultiplexer_1_out5),
    .out6(demultiplexer_1_out6), .out7(demultiplexer_1_out7), .out8(demultiplexer_1_out8),
    .out9(demultiplexer_1_out9), .out10(demultiplexer_1_out10), .out11(demultiplexer_1_out11),
    .out12(demultiplexer_1_out12), .out13(demultiplexer_1_out13), .out14(demultiplexer_1_out14),
    .out15(demultiplexer_1_out15), .in(write), .sel(write_select));  // open: en
  Registrador registrador_1 (.ENTRADA(Data_IN), .CLOCK(demultiplexer_1_out0), .\SAÍDA (\registrador_1_saída ));
  Registrador registrador_2 (.ENTRADA(Data_IN), .CLOCK(demultiplexer_1_out1), .\SAÍDA (\registrador_2_saída ));
  Registrador registrador_3 (.ENTRADA(Data_IN), .CLOCK(demultiplexer_1_out2), .\SAÍDA (\registrador_3_saída ));
  Registrador registrador_4 (.ENTRADA(Data_IN), .CLOCK(demultiplexer_1_out3), .\SAÍDA (\registrador_4_saída ));
  Registrador registrador_5 (.ENTRADA(Data_IN), .CLOCK(demultiplexer_1_out4), .\SAÍDA (\registrador_5_saída ));
  Registrador registrador_6 (.ENTRADA(Data_IN), .CLOCK(demultiplexer_1_out5), .\SAÍDA (\registrador_6_saída ));
  Registrador registrador_7 (.ENTRADA(Data_IN), .CLOCK(demultiplexer_1_out6), .\SAÍDA (\registrador_7_saída ));
  Registrador registrador_8 (.ENTRADA(Data_IN), .CLOCK(demultiplexer_1_out7), .\SAÍDA (\registrador_8_saída ));
  Registrador registrador_9 (.ENTRADA(Data_IN), .CLOCK(demultiplexer_1_out8), .\SAÍDA (\registrador_9_saída ));
  Registrador registrador_10 (.ENTRADA(Data_IN), .CLOCK(demultiplexer_1_out9), .\SAÍDA (\registrador_10_saída ));
  Registrador registrador_11 (.ENTRADA(Data_IN), .CLOCK(demultiplexer_1_out10), .\SAÍDA (\registrador_11_saída ));
  Registrador registrador_12 (.ENTRADA(Data_IN), .CLOCK(demultiplexer_1_out11), .\SAÍDA (\registrador_12_saída ));
  Registrador registrador_13 (.ENTRADA(Data_IN), .CLOCK(demultiplexer_1_out12), .\SAÍDA (\registrador_13_saída ));
  Registrador registrador_14 (.ENTRADA(Data_IN), .CLOCK(demultiplexer_1_out13), .\SAÍDA (\registrador_14_saída ));
  Registrador registrador_15 (.ENTRADA(Data_IN), .CLOCK(demultiplexer_1_out14), .\SAÍDA (\registrador_15_saída ));
  Registrador registrador_16 (.ENTRADA(Data_IN), .CLOCK(demultiplexer_1_out15), .\SAÍDA (\registrador_16_saída ));
  Multiplexer #(.select(4), .width(8)) multiplexer_1 (
    .in0(\registrador_1_saída ), .in1(\registrador_2_saída ), .in2(\registrador_3_saída ),
    .in3(\registrador_4_saída ), .in4(\registrador_5_saída ), .in5(\registrador_6_saída ),
    .in6(\registrador_7_saída ), .in7(\registrador_8_saída ), .in8(\registrador_9_saída ),
    .in9(\registrador_10_saída ), .in10(\registrador_11_saída ), .in11(\registrador_12_saída ),
    .in12(\registrador_13_saída ), .in13(\registrador_14_saída ), .in14(\registrador_15_saída ),
    .in15(\registrador_16_saída ), .out(Rx), .sel(Rx_Select));  // open: en
  Multiplexer #(.select(4), .width(8)) multiplexer_2 (
    .in0(\registrador_1_saída ), .in1(\registrador_2_saída ), .in2(\registrador_3_saída ),
    .in3(\registrador_4_saída ), .in4(\registrador_5_saída ), .in5(\registrador_6_saída ),
    .in6(\registrador_7_saída ), .in7(\registrador_8_saída ), .in8(\registrador_9_saída ),
    .in9(\registrador_10_saída ), .in10(\registrador_11_saída ), .in11(\registrador_12_saída ),
    .in12(\registrador_13_saída ), .in13(\registrador_14_saída ), .in14(\registrador_15_saída ),
    .in15(\registrador_16_saída ), .out(Ry), .sel(Ry_Select));  // open: en
endmodule
